# Fritzing sketch WaterPump_5V (saved by Fritzing 0.9.3b)
breadboards: 1

parts:
  Part1 = Arduino Uno (Rev3)
  M1 = DC Motor
  R1 = Resistor [tolerance=±5% resistance=220 package="2010 [SMD]"]
  R2 = Resistor [tolerance=±5% resistance=10k package="2010 [SMD]"]
  Q1 = MOSFET-NCHANNEL [package=to220v]
  D1 = Schottky Diode [part_number=1N5817 package="300 mil [THT]"]  # not connected
  Power_plug1 = Power plug

nets:
  N1: Part1.D9_PWM, R1.Pin_0
  GND: Part1.GND, R2.Pin_0, Q1.S, Power_plug1.GND
  N2: M1.pin_1, Power_plug1.VCC
  N3: M1.pin_2, Q1.D
  N4: R1.Pin_1, R2.Pin_1, Q1.G

notes:
  WATER PUMP 5V
  POWER SUPPLY
  5V 1A (or higher)
  COMPONENTS:
  - N-channel MOSFET IRLZ44N
  - 10K ohms resistor
  - 220 ohms resistor
  - 1N4001 diode
  CAUTION!
  A diode has polarity — the end marked with a band corresponds to the negative (cathode) side.
